// Digital circuit 2bit_counter.dig as structural Verilog
module _2bit_counter (
  input  En,
  input  D0,
  input  D1,
  input  Load,
  input  Clock,
  output Q0,
  output Q1
);

  wire and_1_out, multiplexer_1_out, multiplexer_2_out, xor_1_out, xor_2_out;

  and and_1 (and_1_out, Q0, En);
  xor xor_1 (xor_1_out, Q0, En);
  xor xor_2 (xor_2_out, Q1, and_1_out);
  Multiplexer multiplexer_1 (.sel(Load), .in_0(xor_1_out), .in_1(D0), .out(multiplexer_1_out));
  Multiplexer multiplexer_2 (.sel(Load), .in_0(xor_2_out), .in_1(D1), .out(multiplexer_2_out));
  D_FF d_ff_1 (.D(multiplexer_1_out), .C(Clock), .Q(Q0));  // open: nQ
  D_FF d_ff_2 (.D(multiplexer_2_out), .C(Clock), .Q(Q1));  // open: nQ
endmodule
