// Digital circuit 4bit_comparator.dig as structural Verilog
module _4bit_comparator (
  input  x0,
  input  x1,
  input  x2,
  input  x3,
  input  y0,
  input  y1,
  input  y2,
  input  y3,
  output x_eq_y
);

  wire xnor_1_out, xnor_2_out, xnor_3_out, xnor_4_out;

  xnor xnor_1 (xnor_1_out, x3, y3);
  xnor xnor_2 (xnor_2_out, x2, y2);
  xnor xnor_3 (xnor_3_out, x1, y1);
  xnor xnor_4 (xnor_4_out, x0, y0);
  and and_1 (x_eq_y, xnor_1_out, xnor_2_out, xnor_3_out, xnor_4_out);
endmodule
