// Digital circuit 4bit_counter.dig as structural Verilog
module _4bit_counter (
  input  Enable,
  input  D0,
  input  D1,
  input  D2,
  input  D3,
  input  Load,
  input  Clock,
  output Q0,
  output Q1,
  output Q2,
  output Q3
);

  wire and_1_out, and_2_out, and_3_out, multiplexer_1_out, multiplexer_2_out, multiplexer_3_out,
       multiplexer_4_out, xor_1_out, xor_2_out, xor_3_out, xor_4_out;

  and and_1 (and_1_out, Q0, Enable);
  and and_2 (and_2_out, Q1, and_1_out);
  and and_3 (and_3_out, Q2, and_2_out);
  xor xor_1 (xor_1_out, Q0, Enable);
  xor xor_2 (xor_2_out, Q1, and_1_out);
  xor xor_3 (xor_3_out, Q2, and_2_out);
  xor xor_4 (xor_4_out, Q3, and_3_out);
  Multiplexer multiplexer_1 (.sel(Load), .in_0(xor_1_out), .in_1(D0), .out(multiplexer_1_out));
  Multiplexer multiplexer_2 (.sel(Load), .in_0(xor_2_out), .in_1(D1), .out(multiplexer_2_out));
  Multiplexer multiplexer_3 (.sel(Load), .in_0(xor_3_out), .in_1(D2), .out(multiplexer_3_out));
  Multiplexer multiplexer_4 (.sel(Load), .in_0(xor_4_out), .in_1(D3), .out(multiplexer_4_out));
  D_FF d_ff_1 (.D(multiplexer_1_out), .C(Clock), .Q(Q0));  // open: nQ
  D_FF d_ff_2 (.D(multiplexer_2_out), .C(Clock), .Q(Q1));  // open: nQ
  D_FF d_ff_3 (.D(multiplexer_3_out), .C(Clock), .Q(Q2));  // open: nQ
  D_FF d_ff_4 (.D(multiplexer_4_out), .C(Clock), .Q(Q3));  // open: nQ
endmodule
