// Digital circuit 8bit_PIPOregister.dig as structural Verilog
module _8bit_PIPOregister (
  input  in_0,
  input  in_1,
  input  in_2,
  input  in_3,
  input  in_4,
  input  in_5,
  input  in_6,
  input  in_7,
  input  clk,
  output out_0,
  output out_1,
  output out_2,
  output out_3,
  output out_4,
  output out_5,
  output out_6,
  output out_7
);

  D_FF d_ff_1 (.D(in_0), .C(clk), .Q(out_0));  // open: nQ
  D_FF d_ff_2 (.D(in_1), .C(clk), .Q(out_1));  // open: nQ
  D_FF d_ff_3 (.D(in_2), .C(clk), .Q(out_2));  // open: nQ
  D_FF d_ff_4 (.D(in_3), .C(clk), .Q(out_3));  // open: nQ
  D_FF d_ff_5 (.D(in_4), .C(clk), .Q(out_4));  // open: nQ
  D_FF d_ff_6 (.D(in_5), .C(clk), .Q(out_5));  // open: nQ
  D_FF d_ff_7 (.D(in_6), .C(clk), .Q(out_6));  // open: nQ
  D_FF d_ff_8 (.D(in_7), .C(clk), .Q(out_7));  // open: nQ
endmodule
