// Digital circuit 8bit_comparator.dig as structural Verilog
module _8bit_comparator (
  input  x0,
  input  x1,
  input  x2,
  input  x3,
  input  x4,
  input  x5,
  input  x6,
  input  x7,
  input  y0,
  input  y1,
  input  y2,
  input  y3,
  input  y4,
  input  y5,
  input  y6,
  input  y7,
  output x_eq_y
);

  wire _4bit_comparator_1_x_eq_y, _4bit_comparator_2_x_eq_y;

  _4bit_comparator _4bit_comparator_1 (
    .x0(x0), .x1(x1), .x2(x2), .x3(x3), .y0(y0), .y1(y1), .y2(y2), .y3(y3), .x_eq_y(_4bit_comparator_1_x_eq_y));
  _4bit_comparator _4bit_comparator_2 (
    .x0(x4), .x1(x5), .x2(x6), .x3(x7), .y0(y4), .y1(y5), .y2(y6), .y3(y7), .x_eq_y(_4bit_comparator_2_x_eq_y));
  and and_1 (x_eq_y, _4bit_comparator_1_x_eq_y, _4bit_comparator_2_x_eq_y);
endmodule
