// Digital circuit attempt_counter_logic.dig as structural Verilog
module attempt_counter_logic (
  input  pw_correct,
  input  clk,
  input  reset,
  output Out
);

  wire and_1_out, and_2_out, and_3_out, and_4_out, not_1_out, or_1_out, or_2_out, or_3_out, y_1_nq, y_1_q,
       y_2_nq, y_2_q;

  and and_1 (and_1_out, y_1_q, y_2_q);
  and and_2 (and_2_out, y_1_nq, y_2_nq);
  and and_3 (and_3_out, y_1_nq, pw_correct);
  or or_1 (or_1_out, and_1_out, and_2_out, and_3_out);
  or or_2 (or_2_out, y_2_q, y_1_q, pw_correct);
  D_FF_AS y_1 (.Set(1'b0), .D(or_2_out), .C(clk), .Clr(reset), .Q(y_1_q), .nQ(y_1_nq));
  D_FF_AS y_2 (.Set(1'b0), .D(or_1_out), .C(clk), .Clr(reset), .Q(y_2_q), .nQ(y_2_nq));
  or or_3 (or_3_out, y_1_nq, y_2_q);
  and and_4 (and_4_out, y_1_q, y_2_q);
  TransGate transgate_1 (.A(or_3_out), .nA(not_1_out), .out1(and_4_out), .out2(Out));
  not not_1 (not_1_out, or_3_out);

  // Notes on the sheet:
  //   Y_2 = y_{1}y_{2} + y'_{1}y'_{2} + y'_{1}pw_correct
  //   Y_1 = y_1 + y_2 + pw_correct
  //   Must be 0 only when in DISABLED
  //   state (10)
  //   STATES:
  //   0 FAIL 	(00)
  //   1 FAIL 	(01)
  //   DISABLED	(10)
  //   UNLOCKED	(11)
endmodule
