// Digital circuit mod3_counter.dig as structural Verilog
module mod3_counter (
  input  En,
  input  Clr,
  input  Clock,
  output Q0,
  output Q1
);

  _2bit_counter _2bit_counter_1 (.En(En), .D0(1'b0), .D1(1'b0), .Load(Clr), .Clock(Clock), .Q0(Q0), .Q1(Q1));
endmodule
