// Digital circuit main_lock_circuit.dig as structural Verilog
module main_lock_circuit (
  input  pw_0,
  input  pw_1,
  input  pw_2,
  input  pw_3,
  input  pw_4,
  input  pw_5,
  input  pw_6,
  input  pw_7,
  input  Send,
  input  mode,
  input  reset,
  input  Clk,
  output Out
);

  wire _8bit_comparator_1_x_eq_y, _8bit_piporegister_1_out_0, _8bit_piporegister_1_out_1,
       _8bit_piporegister_1_out_2, _8bit_piporegister_1_out_3, _8bit_piporegister_1_out_4,
       _8bit_piporegister_1_out_5, _8bit_piporegister_1_out_6, _8bit_piporegister_1_out_7, and_1_out,
       and_2_out, and_3_out, and_4_out, d_ff_1_nq, not_1_out, not_2_out;

  and and_1 (and_1_out, Send, not_1_out);
  not not_1 (not_1_out, Clk);
  and and_2 (and_2_out, mode, Clk);
  D_FF d_ff_1 (.D(and_1_out), .C(Clk), .nQ(d_ff_1_nq));  // open: Q
  _8bit_PIPOregister _8bit_piporegister_1 (
    .in_0(pw_0), .in_1(pw_1), .in_2(pw_2), .in_3(pw_3), .in_4(pw_4), .in_5(pw_5), .in_6(pw_6), .in_7(pw_7),
    .clk(and_2_out), .out_0(_8bit_piporegister_1_out_0), .out_1(_8bit_piporegister_1_out_1),
    .out_2(_8bit_piporegister_1_out_2), .out_3(_8bit_piporegister_1_out_3),
    .out_4(_8bit_piporegister_1_out_4), .out_5(_8bit_piporegister_1_out_5),
    .out_6(_8bit_piporegister_1_out_6), .out_7(_8bit_piporegister_1_out_7));
  and and_3 (and_3_out, and_1_out, d_ff_1_nq);
  _8bit_comparator _8bit_comparator_1 (
    .x0(_8bit_piporegister_1_out_0), .x1(_8bit_piporegister_1_out_1), .x2(_8bit_piporegister_1_out_2),
    .x3(_8bit_piporegister_1_out_3), .x4(_8bit_piporegister_1_out_4), .x5(_8bit_piporegister_1_out_5),
    .x6(_8bit_piporegister_1_out_6), .x7(_8bit_piporegister_1_out_7), .y0(pw_0), .y1(pw_1), .y2(pw_2),
    .y3(pw_3), .y4(pw_4), .y5(pw_5), .y6(pw_6), .y7(pw_7), .x_eq_y(_8bit_comparator_1_x_eq_y));
  not not_2 (not_2_out, mode);
  and and_4 (and_4_out, not_2_out, Clk, and_3_out);
  attempt_counter_logic attempt_counter_logic_1 (
    .pw_correct(_8bit_comparator_1_x_eq_y), .clk(and_4_out), .reset(reset), .Out(Out));

  // Notes on the sheet:
  //   mode: Normal Mode 	         = 0
  //   Programming Mode = 1
  //   Clk: Hz: 50
  //   8BIT PIPO REGISTER
endmodule
